// Digital circuit control.dig as structural Verilog
module control (
  input  [15:0] Instr,
  input  En,
  output [3:0] RT,
  output RTW,
  output [3:0] RA,
  output [3:0] AluOp,
  output AluD,
  output [7:0] Imm,
  output LoD,
  output HiD,
  output Jmp,
  output [3:0] JT,
  output JLD
);

  wire _0_3RA, _0_7Imm, _8_11JT, _8_11RT, HiD_t, LoD_t, RTW_t;
  wire [3:0] AluOp_t, JT_t, RA_t, RT_t;
  wire [7:0] Imm_t;

  assign JT_t = _8_11JT ? Instr[11:8] : 4'bz;  // Driver driver_1
  assign AluOp_t = _0_3RA ? Instr[11:8] : 4'bz;  // Driver driver_2
  assign RT_t = _8_11RT ? Instr[11:8] : 4'bz;  // Driver driver_3
  assign RT_t = _0_3RA ? Instr[7:4] : 4'bz;  // Driver driver_4
  Decoder #(.Selector_Bits(4)) decoder_1 (
    .sel(Instr[15:12]), .out_1(_0_3RA), .out_2(LoD_t), .out_3(HiD_t), .out_4(_8_11JT));  // open: out_0, out_5, out_6, out_7, out_8, out_9, out_10, out_11, out_12, out_13, out_14, out_15
  or or_1 (_8_11RT, LoD_t, HiD_t);
  or or_2 (RTW_t, _0_3RA, LoD_t, HiD_t);
  or or_3 (_0_7Imm, LoD_t, HiD_t, _8_11JT);
  assign Imm_t = _0_7Imm ? Instr[7:0] : 8'bz;  // Driver driver_5
  assign RA_t = _0_3RA ? Instr[3:0] : 4'bz;  // Driver driver_6
  assign RT = En ? RT_t : 4'bz;  // Driver driver_7
  and and_1 (RTW, RTW_t, En);
  assign RA = En ? RA_t : 4'bz;  // Driver driver_8
  assign AluOp = En ? AluOp_t : 4'bz;  // Driver driver_9
  and and_2 (AluD, _0_3RA, En);
  assign Imm = En ? Imm_t : 8'bz;  // Driver driver_10
  and and_3 (LoD, LoD_t, En);
  and and_4 (HiD, HiD_t, En);
  and and_5 (Jmp, _8_11JT, En);
  assign JT = En ? JT_t : 4'bz;  // Driver driver_11
  and and_6 (JLD, _8_11JT, En);

  // Other names for the same wires on the sheet: _4_7RT = _0_3RA; _8_11AluOp = _0_3RA; AluD_t = _0_3RA;
  //   JLD_t = _8_11JT; Jmp_t = _8_11JT

  // Notes on the sheet:
  //   RT: Address of target register
  //   RTW: Address of target register
  //   RA: Address of argument register
  //   AluOp: ALU operation to perform
  //   En: Enabled when on
  //   AluD: High when ALU result should be sent to data bus
  //   Imm: 8 bit immediate value
  //   LoD: Write target with low bits set to Imm to data
  //   HiD: Write target with high bits set to Imm to data
  //   Jmp: When high, jump if jump decider is true
  //   JT: Four bit jump type
  //   JLD: When high, write jump location to data bus
endmodule
